# Fritzing sketch Untitled_Sketch (saved by Fritzing 0.9.3b)

parts:
  Composant1 = Arduino Uno (Rev3)
  SPKR3 = Loudspeaker
  Composant2 = Arduino Mega 2560 (Rev3)
  Composant3 = Arduino Nano (Rev3.0)
  SdModule1 = SdModule
  SdModule2 = SdModule
  SdModule3 = SdModule
  SPKR4 = Loudspeaker
  SPKR5 = Loudspeaker

nets:
  N1: Composant1.D9_PWM, SPKR4.pin2
  N2: Composant1.D11_PWM/MOSI, SdModule1.MOSI
  N3: Composant1.D12/MISO, SdModule1.MISO
  N4: Composant1.D13/SCK, SdModule1.SCK
  GND: Composant1.GND, SdModule1.GND, SPKR4.pin1
  N5: Composant1.D4, SdModule1.SS
  5V: Composant1.5V, SdModule1.5V
  GND_2: SPKR3.pin1, Composant3.GND, SdModule3.GND
  N6: SPKR3.pin2, Composant3.D9
  GND_3: Composant2.GND, SdModule2.GND, SPKR5.pin1
  N7: Composant2.D13_PWM, SdModule2.SCK
  N8: Composant2.D12_PWM, SdModule2.MISO
  N9: Composant2.D11_PWM, SdModule2.MOSI
  5V_2: Composant2.5V, SdModule2.5V
  N10: Composant2.D4_PWM, SdModule2.SS
  N11: Composant2.D46, SPKR5.pin2
  N12: Composant3.D4, SdModule3.SS
  N13: Composant3.D11/MOSI, SdModule3.MOSI
  N14: Composant3.D12/MISO, SdModule3.MISO
  5V_3: Composant3.5V, SdModule3.5V
  N15: Composant3.D13/SCK, SdModule3.SCK
